# Fritzing sketch Diagram (saved by Fritzing 1.0.4)
breadboards: 1

parts:
  Mod1 = Amica NodeMCU DEVKIT 1.0
  HC-SR04_Sensor_1 = HC-SR04 Ultrasonic Distance Sensor
  LED1 = smd LED [color="Red (660nm)" package="1206 [SMD]"]
  LED2 = smd LED [color="Yellow (595nm)" package="1206 [SMD]"]
  LED3 = smd LED [color="Green (565nm)" package="1206 [SMD]"]
  LED4 = smd LED [color="Blue (505nm)" package="1206 [SMD]"]
  R1 = Resistor [tolerance=±5% power=0.25W resistance=330M package=THT]
  R2 = Resistor [tolerance=±5% power=0.25W resistance=330M package=THT]
  R3 = Resistor [tolerance=±5% power=0.25W resistance=330M package=THT]
  R4 = Resistor [tolerance=±5% power=0.25W resistance=330M package=THT]

nets:
  N1: Mod1.pin1, Mod1.pin_10, Mod1.pin_26, HC-SR04_Sensor_1.VCC
  N2: Mod1.pin2, Mod1.pin_9, Mod1.pin_25, Mod1.pin_29, HC-SR04_Sensor_1.GND, LED1.cathode, LED2.cathode, LED3.cathode, LED4.cathode
  N3: Mod1.pin6, R4.Pin_1
  N4: Mod1.pin7, R3.Pin_1
  N5: Mod1.pin8, R1.Pin_1
  N6: Mod1.pin_12, R2.Pin_1
  N7: Mod1.pin_13, HC-SR04_Sensor_1.ECHO
  N8: Mod1.pin_14, HC-SR04_Sensor_1.TRIG
  N9: LED1.anode, R1.Pin_0
  N10: LED2.anode, R3.Pin_0
  N11: LED3.anode, R4.Pin_0
  N12: LED4.anode, R2.Pin_0
